// Logisim project RiscVComputer.before-cpus.circ as structural Verilog: 9 circuits, main circuit main
module main (
  input  RESET
);

  wire ALUSrc, branch_taken, CLK, IsBranch, MemRead, MemWrite, RegWrite;
  wire [1:0] ALUOp;
  wire [2:0] funct3, ImmSel;
  wire [3:0] ALUCtrl;
  wire [4:0] rd, rs1, rs2;
  wire [6:0] funct7, opcode;
  wire [31:0] adder_1_out, adder_2_out, alu_1_result, alu_b, imm, instr, memory_1_read_data,
       multiplexer_2_out, next_pc, PC, register_1_q, registerfile_1_rs1_data, registerfile_1_rs2_data,
       rom_1_data, rs1_data, rs2_data, undriven, wb_data;

  Clock clock_1 (.out(CLK));
  Register #(.width(32)) register_1 (.D(next_pc), .en(1'b1), .clk(CLK), .Q(register_1_q), .clr(RESET));
  ROM #(.dataWidth(32)) rom_1 (.addr(register_1_q[9:2]), .data(rom_1_data));
  Adder #(.width(32)) adder_1 (.a(32'h4), .b(PC), .out(adder_1_out));  // open: cin, cout
  Adder #(.width(32)) adder_2 (.a(PC), .b(alu_b), .out(adder_2_out));  // open: cin, cout
  Multiplexer #(.width(32)) multiplexer_1 (.in0(adder_1_out), .in1(adder_2_out), .out(next_pc), .sel(branch_taken));
  // Probe on instr
  InstructionDecode instructiondecode_1 (
    .Instruction(rom_1_data), .funct7(funct7), .rs2(rs2), .rs1(rs1), .funct3(funct3), .rd(rd), .opcode(opcode));
  MainControl maincontrol_1 (
    .opcode(opcode), .RegWrite(RegWrite), .ALUSrc(ALUSrc), .MemWrite(MemWrite), .IsBranch(IsBranch),
    .ALUOp(ALUOp), .ImmSel(ImmSel), .MemRead(MemRead));
  RegisterFile registerfile_1 (
    .write_data(wb_data), .CLK(CLK), .write(RegWrite), .rd(rd), .rs1(rs1), .rs2(rs2),
    .rs1_data(registerfile_1_rs1_data), .rs2_data(registerfile_1_rs2_data));
  ImmGen immgen_1 (.Instruction(instr), .ImmSel(ImmSel), .Imm(imm));
  ALUControl alucontrol_1 (.funct7(funct7), .ALUOp(ALUOp), .funct3(funct3), .ALUCtrl(ALUCtrl));
  Multiplexer #(.width(32)) multiplexer_2 (
    .in0(registerfile_1_rs2_data), .in1(imm), .out(multiplexer_2_out), .sel(ALUSrc));
  ALU alu_1 (
    .rs1_data(registerfile_1_rs1_data), .rs2_data(multiplexer_2_out), .ALU_Ctrl(ALUCtrl),
    .result(alu_1_result));
  BranchUnit branchunit_1 (
    .rs1_data(rs1_data), .rs2_data(rs2_data), .IsBranch(IsBranch), .funct3(funct3),
    .branch_taken(branch_taken));
  Memory memory_1 (
    .Address(alu_1_result), .write_data(rs2_data), .MemWrite(MemWrite), .MemRead(MemRead), .CLK(CLK),
    .funct3(funct3), .read_data(memory_1_read_data));
  Multiplexer #(.width(32)) multiplexer_3 (.in0(undriven), .in1(memory_1_read_data), .out(wb_data), .sel(MemRead));

  // Notes on the sheet:
  //   Clock (use Simulate > Tick)
  //   PC register
  //   RESET: 1 = PC back to 0
  //   alu_b = imm when IsBranch
  //   How to run
  //   1. Load a program into the ROM (right click > Edit Contents).
  //   2. Poke RESET to 1 then 0, then use Simulate > Tick Full Cycle once per instruction.
  //   3. Watch PC, instr, and registers (open RegisterFile from the Poke tool).
  //   Supported: R-type, I-type ALU, lw/lb/lbu, sw, beq, bne.
  //   Not wired yet: JAL, JALR, LUI, AUIPC (MainControl already decodes them).
  //   IF - Instruction Fetch
  //   contents of rom_1 (hex, n*v repeats v):
  //   208463 42a303 63a523 208663 208663 208663
  //   Next-PC logic
  //   PC + 4
  //   PC + branch offset
  //   Instruction ROM 256 x 32 (addr = PC[9:2])
  //   0: PC+4   1: branch
  //   sel = branch_taken
  //   instr (hex)
  //   InstructionDecode: cuts instr into fields
  //   Control unit
  //   MainControl: opcode > control signals
  //   RV32I single-cycle CPU - top level
  //   Data flows left to right: IF > ID > EX > MEM > WB.  Tunnels with the same name are the same wire.
  //   ID - Decode / Register Read
  //   RegisterFile: x0..x31, 2 read ports, 1 write port
  //   ImmGen: immediate (I/S/B/U/J)
  //   ALUControl: ALUOp + funct > ALUCtrl
  //   ALU input B
  //   0: rs2   1: imm
  //   EX - Execute
  //   ALU
  //   BranchUnit: beq / bne
  //   alu_result (address / ALU value)
  //   MEM - Data Memory
  //   Memory: load/store, data RAM
  //   WB
  //   0: ALU   1: memory
endmodule

module ALU (
  input  [31:0] rs1_data,
  input  [31:0] rs2_data,
  input  [3:0] ALU_Ctrl,
  output [31:0] result
);

  wire comparator_1_lt, comparator_2_lt;
  wire [31:0] adder_1_out, and_1_out, bit_extender_1_out, bit_extender_2_out, or_1_out, shifter_1_out,
       shifter_2_out, shifter_3_out, subtractor_1_out, xor_1_out;

  Adder #(.width(32)) adder_1 (.a(rs1_data), .b(rs2_data), .out(adder_1_out));  // open: cin, cout
  Subtractor #(.width(32)) subtractor_1 (.a(rs1_data), .b(rs2_data), .out(subtractor_1_out));  // open: bin, bout
  Shifter #(.width(32)) shifter_1 (.in(rs1_data), .\dist (rs2_data[4:0]), .out(shifter_1_out));
  Shifter #(.shift("lr"), .width(32)) shifter_2 (.in(rs1_data), .\dist (rs2_data[4:0]), .out(shifter_2_out));
  Shifter #(.shift("ar"), .width(32)) shifter_3 (.in(rs1_data), .\dist (rs2_data[4:0]), .out(shifter_3_out));
  Comparator #(.width(32)) comparator_1 (.a(rs1_data), .b(rs2_data), .lt(comparator_1_lt));  // open: gt, eq
  Comparator #(.mode("unsigned"), .width(32)) comparator_2 (
    .a(rs1_data), .b(rs2_data), .lt(comparator_2_lt));  // open: gt, eq
  assign and_1_out = rs1_data & rs2_data;  // AND_Gate and_1, 32 bits wide
  assign or_1_out = rs1_data | rs2_data;  // OR_Gate or_1, 32 bits wide
  assign xor_1_out = rs1_data ^ rs2_data;  // XOR_Gate xor_1, 32 bits wide
  assign bit_extender_1_out = {{31{1'b0}}, comparator_1_lt};  // Bit_Extender bit_extender_1
  assign bit_extender_2_out = {{31{1'b0}}, comparator_2_lt};  // Bit_Extender bit_extender_2
  Multiplexer #(.select(4), .width(32)) multiplexer_1 (
    .in0(adder_1_out), .in1(subtractor_1_out), .in2(and_1_out), .in3(or_1_out), .in4(xor_1_out),
    .in5(shifter_1_out), .in6(shifter_2_out), .in7(shifter_3_out), .in8(bit_extender_1_out),
    .in9(bit_extender_2_out), .out(result), .sel(ALU_Ctrl));  // open: in10, in11, in12, in13, in14, in15
  // Probe on result

  // Notes on the sheet:
  //   ALU
  //   Every operation is computed in parallel; ALU_Ctrl selects which result leaves the ALU.
  //   ADD   (ctrl 0)
  //   SUB   (ctrl 1)
  //   AND   (ctrl 2)
  //   OR   (ctrl 3)
  //   XOR   (ctrl 4)
  //   SLL   (ctrl 5)  A << B[4:0]
  //   SRL   (ctrl 6)  A >> B[4:0]
  //   SRA   (ctrl 7)  A >>> B[4:0]
  //   SRA: arithmetic shift right
  //   SLT
  //   SLTU
  //   ALU_Ctrl  operation
  //   0 ADD   1 SUB   2 AND   3 OR   4 XOR
  //   5 SLL   6 SRL   7 SRA
  //   8 SLT (signed)   9 SLTU (unsigned)
  //   SLT and SLTU: the 1-bit compare result is zero-extended,
  //   so the ALU output is 0x00000000 or 0x00000001.
endmodule

module InstructionDecode (
  input  [31:0] Instruction,
  output [6:0] funct7,
  output [4:0] rs2,
  output [4:0] rs1,
  output [2:0] funct3,
  output [4:0] rd,
  output [6:0] opcode
);


  assign funct3 = Instruction[14:12];
  assign funct7 = Instruction[31:25];
  assign opcode = Instruction[6:0];
  assign rd = Instruction[11:7];
  assign rs1 = Instruction[19:15];
  assign rs2 = Instruction[24:20];

  // Notes on the sheet:
  //   InstructionDecode
  //   Pure wiring (one splitter): cuts the 32-bit instruction into its RISC-V fields.
  //   Field = instruction bits  ->  used by
  //   opcode = instr[6:0]  ->  MainControl (what kind of instruction)
  //   rd = instr[11:7]  ->  RegisterFile write address
  //   funct3 = instr[14:12]  ->  ALUControl, BranchUnit, Memory
  //   rs1 = instr[19:15]  ->  RegisterFile read address 1
  //   rs2 = instr[24:20]  ->  RegisterFile read address 2
  //   funct7 = instr[31:25]  ->  ALUControl (ADD vs SUB, SRL vs SRA)
endmodule

module RegisterFile (
  input  [31:0] write_data,
  input  CLK,
  input  write,
  input  [4:0] rd,
  input  [4:0] rs1,
  input  [4:0] rs2,
  output [31:0] rs1_data,
  output [31:0] rs2_data
);

  wire demultiplexer_1_out0, WE0, WE1, WE2, WE3, WE4, WE5, WE6, WE7, WE8, WE9, WE10, WE11, WE12, WE13, WE14,
       WE15, WE16, WE17, WE18, WE19, WE20, WE21, WE22, WE23, WE24, WE25, WE26, WE27, WE28, WE29, WE30, WE31;
  wire [31:0] X0, X1, X2, X3, X4, X5, X6, X7, X8, X9, X10, X11, X12, X13, X14, X15, X16, X17, X18, X19, X20,
       X21, X22, X23, X24, X25, X26, X27, X28, X29, X30, X31;

  Register #(.width(32)) register_1 (.D({32{1'b0}}), .en(WE0), .clk(CLK), .Q(X0));  // open: clr
  Register #(.width(32)) register_2 (.D(write_data), .en(WE1), .clk(CLK), .Q(X1));  // open: clr
  Register #(.width(32)) register_3 (.D(write_data), .en(WE2), .clk(CLK), .Q(X2));  // open: clr
  Register #(.width(32)) register_4 (.D(write_data), .en(WE3), .clk(CLK), .Q(X3));  // open: clr
  Register #(.width(32)) register_5 (.D(write_data), .en(WE4), .clk(CLK), .Q(X4));  // open: clr
  Register #(.width(32)) register_6 (.D(write_data), .en(WE5), .clk(CLK), .Q(X5));  // open: clr
  Register #(.width(32)) register_7 (.D(write_data), .en(WE6), .clk(CLK), .Q(X6));  // open: clr
  Register #(.width(32)) register_8 (.D(write_data), .en(WE7), .clk(CLK), .Q(X7));  // open: clr
  Multiplexer #(.select(5), .width(32)) multiplexer_1 (
    .in0(X0), .in1(X1), .in2(X2), .in3(X3), .in4(X4), .in5(X5), .in6(X6), .in7(X7), .in8(X8), .in9(X9),
    .in10(X10), .in11(X11), .in12(X12), .in13(X13), .in14(X14), .in15(X15), .in16(X16), .in17(X17),
    .in18(X18), .in19(X19), .in20(X20), .in21(X21), .in22(X22), .in23(X23), .in24(X24), .in25(X25),
    .in26(X26), .in27(X27), .in28(X28), .in29(X29), .in30(X30), .in31(X31), .out(rs1_data), .sel(rs1));
  Register #(.width(32)) register_9 (.D(write_data), .en(WE8), .clk(CLK), .Q(X8));  // open: clr
  Register #(.width(32)) register_10 (.D(write_data), .en(WE9), .clk(CLK), .Q(X9));  // open: clr
  Register #(.width(32)) register_11 (.D(write_data), .en(WE10), .clk(CLK), .Q(X10));  // open: clr
  Register #(.width(32)) register_12 (.D(write_data), .en(WE11), .clk(CLK), .Q(X11));  // open: clr
  Register #(.width(32)) register_13 (.D(write_data), .en(WE12), .clk(CLK), .Q(X12));  // open: clr
  Register #(.width(32)) register_14 (.D(write_data), .en(WE13), .clk(CLK), .Q(X13));  // open: clr
  Register #(.width(32)) register_15 (.D(write_data), .en(WE14), .clk(CLK), .Q(X14));  // open: clr
  Register #(.width(32)) register_16 (.D(write_data), .en(WE15), .clk(CLK), .Q(X15));  // open: clr
  Multiplexer #(.select(5), .width(32)) multiplexer_2 (
    .in0(X0), .in1(X1), .in2(X2), .in3(X3), .in4(X4), .in5(X5), .in6(X6), .in7(X7), .in8(X8), .in9(X9),
    .in10(X10), .in11(X11), .in12(X12), .in13(X13), .in14(X14), .in15(X15), .in16(X16), .in17(X17),
    .in18(X18), .in19(X19), .in20(X20), .in21(X21), .in22(X22), .in23(X23), .in24(X24), .in25(X25),
    .in26(X26), .in27(X27), .in28(X28), .in29(X29), .in30(X30), .in31(X31), .out(rs2_data), .sel(rs2));
  Register #(.width(32)) register_17 (.D(write_data), .en(WE16), .clk(CLK), .Q(X16));  // open: clr
  Register #(.width(32)) register_18 (.D(write_data), .en(WE17), .clk(CLK), .Q(X17));  // open: clr
  Register #(.width(32)) register_19 (.D(write_data), .en(WE18), .clk(CLK), .Q(X18));  // open: clr
  Register #(.width(32)) register_20 (.D(write_data), .en(WE19), .clk(CLK), .Q(X19));  // open: clr
  Register #(.width(32)) register_21 (.D(write_data), .en(WE20), .clk(CLK), .Q(X20));  // open: clr
  Register #(.width(32)) register_22 (.D(write_data), .en(WE21), .clk(CLK), .Q(X21));  // open: clr
  Register #(.width(32)) register_23 (.D(write_data), .en(WE22), .clk(CLK), .Q(X22));  // open: clr
  Register #(.width(32)) register_24 (.D(write_data), .en(WE23), .clk(CLK), .Q(X23));  // open: clr
  Demultiplexer #(.select(5)) demultiplexer_1 (
    .out0(demultiplexer_1_out0), .out1(WE1), .out2(WE2), .out3(WE3), .out4(WE4), .out5(WE5), .out6(WE6),
    .out7(WE7), .out8(WE8), .out9(WE9), .out10(WE10), .out11(WE11), .out12(WE12), .out13(WE13), .out14(WE14),
    .out15(WE15), .out16(WE16), .out17(WE17), .out18(WE18), .out19(WE19), .out20(WE20), .out21(WE21),
    .out22(WE22), .out23(WE23), .out24(WE24), .out25(WE25), .out26(WE26), .out27(WE27), .out28(WE28),
    .out29(WE29), .out30(WE30), .out31(WE31), .in(write), .sel(rd));
  Register #(.width(32)) register_25 (.D(write_data), .en(WE24), .clk(CLK), .Q(X24));  // open: clr
  Register #(.width(32)) register_26 (.D(write_data), .en(WE25), .clk(CLK), .Q(X25));  // open: clr
  Register #(.width(32)) register_27 (.D(write_data), .en(WE26), .clk(CLK), .Q(X26));  // open: clr
  Register #(.width(32)) register_28 (.D(write_data), .en(WE27), .clk(CLK), .Q(X27));  // open: clr
  Register #(.width(32)) register_29 (.D(write_data), .en(WE28), .clk(CLK), .Q(X28));  // open: clr
  Register #(.width(32)) register_30 (.D(write_data), .en(WE29), .clk(CLK), .Q(X29));  // open: clr
  Register #(.width(32)) register_31 (.D(write_data), .en(WE30), .clk(CLK), .Q(X30));  // open: clr
  Register #(.width(32)) register_32 (.D(write_data), .en(WE31), .clk(CLK), .Q(X31));  // open: clr

  // Other names for the same wires on the sheet: wb_data[31:0] = write_data

  // Notes on the sheet:
  //   Read port 1: x[rs1] -> rs1_data
  //   RegisterFile
  //   32 registers x 32 bits. x0 always loads the constant 0, so it always reads 0.
  //   Write: wb_data goes to every register; the DMX turns on only WE[rd] when write = 1.
  //   Read: two 32:1 multiplexers pick x[rs1] and x[rs2] (asynchronous, no clock needed).
  //   Read port 2: x[rs2] -> rs2_data
  //   Write decoder: rd -> WE of one register
endmodule

module ImmGen (
  input  [31:0] Instruction,
  input  [2:0] ImmSel,
  output [31:0] Imm
);

  wire [31:0] bit_extender_1_out, bit_extender_2_out, bit_extender_3_out, bit_extender_4_out;

  assign bit_extender_1_out = {{20{Instruction[31]}}, Instruction[31:20]};  // Bit_Extender bit_extender_1
  assign bit_extender_2_out = {{20{Instruction[31]}}, {Instruction[31:25], Instruction[11:7]}};  // Bit_Extender bit_extender_2
  assign bit_extender_3_out = {{19{Instruction[31]}}, {Instruction[31], Instruction[7], Instruction[30:25], Instruction[11:8], 1'b0}};  // Bit_Extender bit_extender_3
  assign bit_extender_4_out = {{11{Instruction[31]}}, {Instruction[31], Instruction[19:12], Instruction[20], Instruction[30:21], 1'b0}};  // Bit_Extender bit_extender_4
  Multiplexer #(.select(3), .width(32)) multiplexer_1 (
    .in0(bit_extender_1_out), .in1(bit_extender_2_out), .in2(bit_extender_3_out),
    .in3({Instruction[31:12], {12{1'b0}}}), .in4(bit_extender_4_out), .out(Imm), .sel(ImmSel));  // open: in5, in6, in7

  // Notes on the sheet:
  //   imm = instr[31:20]
  //   imm = instr[31:25], instr[11:7]
  //   imm = instr[31], [7], [30:25], [11:8], 0
  //   imm = instr[31:12] << 12
  //   low 12 bits are zero (12 zero bits appended)
  //   imm = instr[31], [19:12], [20], [30:21], 0
  //   bit 0 is always 0 (offsets are even)
  //   I-type
  //   S-type
  //   B-type
  //   U-type
  //   J-type
  //   ImmGen
  //   Rebuilds the 32-bit immediate from the instruction bits; ImmSel picks the format.
  //   ImmSel: 0 I   1 S   2 B   3 U   4 J
  //   All results are sign-extended to 32 bits.
endmodule

module MainControl (
  input  [6:0] opcode,
  output RegWrite,
  output ALUSrc,
  output MemWrite,
  output IsBranch,
  output [1:0] ALUOp,
  output [2:0] ImmSel,
  output MemRead
);

  wire IsImm, IsJALR, IsLui, IsR, or_6_out;

  Comparator #(.width(7)) comparator_1 (.a(opcode), .b(7'b0110011), .eq(IsR));  // open: gt, lt
  Comparator #(.width(7)) comparator_2 (.a(opcode), .b(7'b0010011), .eq(IsImm));  // open: gt, lt
  Comparator #(.width(7)) comparator_3 (.a(opcode), .b(7'b0000011), .eq(MemRead));  // open: gt, lt
  Comparator #(.width(7)) comparator_4 (.a(opcode), .b(7'b0100011), .eq(MemWrite));  // open: gt, lt
  Comparator #(.width(7)) comparator_5 (.a(opcode), .b(7'b1100011), .eq(IsBranch));  // open: gt, lt
  Comparator #(.width(7)) comparator_6 (.a(opcode), .b(7'b0110111), .eq(IsLui));  // open: gt, lt
  Comparator #(.width(7)) comparator_7 (.a(opcode), .b(7'b1101111), .eq(ImmSel[2]));  // open: gt, lt
  Comparator #(.width(7)) comparator_8 (.a(opcode), .b(7'b1100111), .eq(IsJALR));  // open: gt, lt
  or or_1 (ImmSel[0], MemWrite, IsLui);
  or or_2 (ALUOp[0], IsBranch, IsImm);
  or or_3 (ALUOp[1], IsImm, IsR);
  or or_4 (ImmSel[1], IsBranch, IsLui);
  or or_5 (RegWrite, IsR, IsImm, MemRead);
  or or_6 (or_6_out, MemRead, IsImm, MemWrite);
  or or_7 (ALUSrc, or_6_out, IsBranch);

  // Other names for the same wires on the sheet: IsJAL = ImmSel[2]; IsLoad = MemRead; IsStore = MemWrite

  // Notes on the sheet:
  //   MainControl
  //   Compares opcode with each instruction class (left) and combines the flags into control signals (right).
  //   11: I-type
  //   00: force add
  //   01: force sub
  //   10: R-type
  //   Control table (checked by simulation)
  //   opcode  class      signals that are 1
  //   0x33 R-type    RegWrite, ALUOp=10
  //   0x13 I-type    RegWrite, ALUSrc, ALUOp=11
  //   0x03 load       RegWrite, ALUSrc, MemRead
  //   0x23 store     ALUSrc, MemWrite, ImmSel=001 (S)
  //   0x63 branch   ALUSrc, IsBranch, ALUOp=01, ImmSel=010 (B)
  //   0x37 LUI        ImmSel=011 (U)    - not wired in main yet
  //   0x6F JAL        ImmSel=100 (J)    - not wired in main yet
  //   0x67 JALR      ImmSel=000 (I)    - not wired in main yet
  //   ImmSel bits: bit0 = IsStore OR IsLui,  bit1 = IsBranch OR IsLui,  bit2 = IsJAL.
  //   ALUSrc = 1 means ALU operand B is the immediate, not rs2.
endmodule

module ALUControl (
  input  [6:0] funct7,
  input  [1:0] ALUOp,
  input  [2:0] funct3,
  output [3:0] ALUCtrl
);

  wire [3:0] multiplexer_1_out, multiplexer_2_out, multiplexer_3_out, multiplexer_4_out;

  Multiplexer #(.width(4)) multiplexer_1 (.in0(4'b0110), .in1(4'b0111), .out(multiplexer_1_out), .sel(funct7[5]));
  Multiplexer #(.width(4)) multiplexer_2 (.in0(4'b0000), .in1(4'b0001), .out(multiplexer_2_out), .sel(funct7[5]));
  Multiplexer #(.select(3), .width(4)) multiplexer_3 (
    .in0(multiplexer_2_out), .in1(4'b0110), .in2(4'b1000), .in3(4'b1001), .in4(4'b0100),
    .in5(multiplexer_1_out), .in6(4'b0011), .in7(4'b0010), .out(multiplexer_3_out), .sel(funct3));
  Multiplexer #(.select(3), .width(4)) multiplexer_4 (
    .in0(4'b0000), .in1(4'b0101), .in2(4'b1000), .in3(4'b1001), .in4(4'b0100), .in5(multiplexer_1_out),
    .in6(4'b0011), .in7(4'b0010), .out(multiplexer_4_out), .sel(funct3));
  Multiplexer #(.select(2), .width(4)) multiplexer_5 (
    .in0(4'b0000), .in1(4'b0001), .in2(multiplexer_3_out), .in3(multiplexer_4_out), .out(ALUCtrl), .sel(ALUOp));

  // Notes on the sheet:
  //   ADDI 0000
  //   SLLI 0101
  //   SLTI 1000
  //   SLTIU 1001
  //   XORI 0100
  //   ANDI 0010
  //   ORI 0011
  //   SRL 0110
  //   SRA 0111
  //   ADD 0000
  //   SUB 0001
  //   SLL 0101
  //   SLT 1000
  //   SLTU 1001
  //   XOR 0100
  //   OR 0011
  //   AND 0010
  //   ALUControl
  //   ALUOp 00 = ADD (load/store)   01 = SUB (branch)   10 = R-type   11 = I-type
  //   R-type and I-type pick the operation from funct3 (funct7 separates ADD/SUB and SRL/SRA).
  //   R-dec
endmodule

module Memory (
  input  [31:0] Address,
  input  [31:0] write_data,
  input  MemWrite,
  input  MemRead,
  input  CLK,
  input  [2:0] funct3,
  output [31:0] read_data
);

  wire [7:0] multiplexer_1_out, ram_1_dout, ram_1_dout_2, ram_1_dout_3, ram_1_dout_4;
  wire [31:0] bit_extender_1_out, bit_extender_2_out;

  RAM #(.dataWidth(32)) ram_1 (
    .addr(Address[9:2]), .we(MemWrite), .oe(MemRead), .clk(CLK), .din(write_data),
    .dout({ram_1_dout_4, ram_1_dout_3, ram_1_dout_2, ram_1_dout}));
  Multiplexer #(.select(2), .width(8)) multiplexer_1 (
    .in0(ram_1_dout), .in1(ram_1_dout_2), .in2(ram_1_dout_3), .in3(ram_1_dout_4), .out(multiplexer_1_out),
    .sel(Address[1:0]));
  assign bit_extender_1_out = {{24{multiplexer_1_out[7]}}, multiplexer_1_out};  // Bit_Extender bit_extender_1
  assign bit_extender_2_out = {{24{1'b0}}, multiplexer_1_out};  // Bit_Extender bit_extender_2
  Multiplexer #(.select(3), .width(32)) multiplexer_2 (
    .in0(bit_extender_1_out), .in2({ram_1_dout_4, ram_1_dout_3, ram_1_dout_2, ram_1_dout}),
    .in4(bit_extender_2_out), .out(read_data), .sel(funct3));  // open: in1, in3, in5, in6, in7

  // Notes on the sheet:
  //   Memory
  //   Data RAM 256 x 32. Stores write a whole word (sw); loads pick lb / lbu / lw with funct3.
  //   funct3  load kind
  //   000 lb   byte, sign-extended
  //   100 lbu  byte, zero-extended
  //   010 lw   whole word
  //   MemWrite: write on clock edge.  MemRead: enable data output.
  //   lw
  //   lb
  //   lbu
endmodule

module BranchUnit (
  input  [31:0] rs1_data,
  input  [31:0] rs2_data,
  input  IsBranch,
  input  [2:0] funct3,
  output branch_taken
);

  wire comparator_1_eq, multiplexer_1_out, not_1_out;

  Comparator #(.width(32)) comparator_1 (.a(rs1_data), .b(rs2_data), .eq(comparator_1_eq));  // open: gt, lt
  not not_1 (not_1_out, comparator_1_eq);
  Multiplexer #(.select(3)) multiplexer_1 (
    .in0(comparator_1_eq), .in1(not_1_out), .out(multiplexer_1_out), .sel(funct3));  // open: in2, in3, in4, in5, in6, in7
  and and_1 (branch_taken, multiplexer_1_out, IsBranch);

  // Notes on the sheet:
  //   BranchUnit
  //   Decides whether a conditional branch is taken.
  //   beq
  //   bne
  //   funct3 = 000 (beq): condition is rs1 == rs2
  //   funct3 = 001 (bne): condition is rs1 != rs2
  //   branch_taken = IsBranch AND condition  ->  selects PC + offset in main
endmodule
